# Fritzing sketch Sketch_V1 (saved by Fritzing 0.9.4)
breadboards: 1

parts:
  Raspberry_Pi_2 = Raspberry Pi 3 [part_number=RPI-3-V1.2]
  Componente2 = Arduino Uno (Rev3) - ICSP
  HC-SR04_Sensor_12 = HC-SR04 Ultrasonic Distance Sensor
  HC-SR04_Sensor_13 = HC-SR04 Ultrasonic Distance Sensor
  HC-SR04_Sensor_11 = HC-SR04 Ultrasonic Distance Sensor
  HC-SR04_Sensor_9 = HC-SR04 Ultrasonic Distance Sensor
  HC-SR04_Sensor_10 = HC-SR04 Ultrasonic Distance Sensor
  HC-SR04_Sensor_6 = HC-SR04 Ultrasonic Distance Sensor
  HC-SR04_Sensor_5 = HC-SR04 Ultrasonic Distance Sensor
  HC-SR04_Sensor_7 = HC-SR04 Ultrasonic Distance Sensor
  HC-SR04_Sensor_8 = HC-SR04 Ultrasonic Distance Sensor
  HC-SR04_Sensor_3 = HC-SR04 Ultrasonic Distance Sensor
  HC-SR04_Sensor_4 = HC-SR04 Ultrasonic Distance Sensor
  HC-SR04_Sensor_2 = HC-SR04 Ultrasonic Distance Sensor
  HC-SR04_Sensor_48 = HC-SR04 Ultrasonic Distance Sensor
  Switch_Ri = Switch with Pull-Up and LED
  Switch_L = Switch with Pull-Up and LED
  L298N4 = L298N DC motor driver
  M7 = DC Motor
  M8 = DC Motor  # not connected
  U8 = LIPO-2000mAh [package=lipo-2000]

nets:
  N1: Raspberry_Pi_2.GPIO2, HC-SR04_Sensor_48.ECHO
  N2: Raspberry_Pi_2.GPIO3, HC-SR04_Sensor_48.TRIG
  N3: Raspberry_Pi_2.GPIO4, HC-SR04_Sensor_2.ECHO
  GND: Raspberry_Pi_2.GND, HC-SR04_Sensor_12.GND, HC-SR04_Sensor_13.GND, HC-SR04_Sensor_11.GND, HC-SR04_Sensor_9.GND, HC-SR04_Sensor_10.GND, HC-SR04_Sensor_6.GND, HC-SR04_Sensor_5.GND, HC-SR04_Sensor_7.GND, HC-SR04_Sensor_8.GND, HC-SR04_Sensor_3.GND, HC-SR04_Sensor_4.GND, HC-SR04_Sensor_2.GND, HC-SR04_Sensor_48.GND
  N4: Raspberry_Pi_2.GPIO17, HC-SR04_Sensor_2.TRIG
  N5: Raspberry_Pi_2.GPIO27, HC-SR04_Sensor_3.ECHO
  N6: Raspberry_Pi_2.GPIO22, HC-SR04_Sensor_3.TRIG
  N7: Raspberry_Pi_2.GPIO10, HC-SR04_Sensor_4.ECHO
  N8: Raspberry_Pi_2.GPIO9, HC-SR04_Sensor_4.TRIG
  N9: Raspberry_Pi_2.GPIO11, HC-SR04_Sensor_5.ECHO
  N10: Raspberry_Pi_2.ID_SD, HC-SR04_Sensor_5.TRIG
  N11: Raspberry_Pi_2.GPIO5, HC-SR04_Sensor_6.ECHO
  N12: Raspberry_Pi_2.GPIO6, HC-SR04_Sensor_6.TRIG
  N13: Raspberry_Pi_2.GPIO13, HC-SR04_Sensor_7.ECHO
  N14: Raspberry_Pi_2.GPIO19, HC-SR04_Sensor_7.TRIG
  N15: Raspberry_Pi_2.GPIO20, HC-SR04_Sensor_13.TRIG
  N16: Raspberry_Pi_2.GPIO16, HC-SR04_Sensor_13.ECHO
  N17: Raspberry_Pi_2.GPIO12, HC-SR04_Sensor_12.TRIG
  N18: Raspberry_Pi_2.ID_SC, HC-SR04_Sensor_12.ECHO
  N19: Raspberry_Pi_2.GPIO7, HC-SR04_Sensor_11.TRIG
  N20: Raspberry_Pi_2.GPIO8, HC-SR04_Sensor_11.ECHO
  N21: Raspberry_Pi_2.GPIO25, HC-SR04_Sensor_10.TRIG
  N22: Raspberry_Pi_2.GPIO24, HC-SR04_Sensor_10.ECHO
  N23: Raspberry_Pi_2.GPIO23, HC-SR04_Sensor_9.TRIG
  N24: Raspberry_Pi_2.GPIO18, HC-SR04_Sensor_9.ECHO
  N25: Raspberry_Pi_2.GPIO15, HC-SR04_Sensor_8.TRIG
  N26: Raspberry_Pi_2.GPIO14, HC-SR04_Sensor_8.ECHO
  VCC: Raspberry_Pi_2.5V, HC-SR04_Sensor_12.VCC, HC-SR04_Sensor_13.VCC, HC-SR04_Sensor_11.VCC, HC-SR04_Sensor_9.VCC, HC-SR04_Sensor_10.VCC, HC-SR04_Sensor_6.VCC, HC-SR04_Sensor_5.VCC, HC-SR04_Sensor_7.VCC, HC-SR04_Sensor_8.VCC, HC-SR04_Sensor_3.VCC, HC-SR04_Sensor_4.VCC, HC-SR04_Sensor_2.VCC, HC-SR04_Sensor_48.VCC
  N27: Componente2.ICSP_MISO, Componente2.D12/MISO, Switch_L.OUT
  GND_2: Componente2.GND, Switch_Ri.GND, Switch_L.GND, L298N4.GND, U8.-
  N28: Componente2.D8, L298N4.IN3
  N29: Componente2.D9_PWM, L298N4.IN2
  N30: Componente2.D10_PWM/SS, L298N4.IN1
  N31: Componente2.D11_PWM/MOSI, L298N4.ENA
  N32: Componente2.D13/SCK, Switch_Ri.OUT
  N33: Componente2.D7, L298N4.IN4
  5V: Componente2.5V, Switch_Ri.VCC, Switch_L.VCC, L298N4.5V
  N34: L298N4.OUT3, M7.pin_2
  N35: L298N4.OUT4, M7.pin_1
  N36: L298N4.12V, U8.+

custom parts:
  L298N DC motor driver: 2x DC motor driver with 78M05 positive voltage regulator (7..35 V) L298N: max 46 V, 2 A Set 5 V Enable jumper to enable 5 V regultor (needed for the L298N) and +5 V output at screw terminal or supply external +5 V at screw terminal Set ENA and/or ENB to +5 V to enable motor permanently or supply ENA and/or ENB with PWM signal IN1 and IN2 set rotation directory for motor A (OUT1/OUT2) IN2 and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
